// Logisim project comp.circ as structural Verilog: 3 circuits, main circuit main
module main (
  input  [3:0] in_1,
  input  in_2,
  input  [3:0] in_3,
  input  [3:0] in_4,
  input  in_5,
  output [7:0] out_6
);

  wire A_In, A_Out, Alu_Mode_1, Alu_Mode_2, Alu_Out, B_In, B_Out, button_1_out, clock_1_out, clock_2_out,
       clock_3_out, clock_4_out, clock_5_out, clock_6_out, clock_7_out, clock_8_out, Count_En, Count_Jump,
       Count_Out, decoder_1_out5, HLT, Instruction_In, Instruction_Out, multiplexer_3_out, not_1_out,
       or_1_out, or_2_out, Output_In, Ram_Adr_In, Ram_Data_In, Ram_Data_Out, RST;
  wire [2:0] counter_1_q;
  wire [3:0] Count, Instructions, multiplexer_1_out, register_3_q, register_4_q;
  wire [7:0] A, alu_1_out_4, B, B_U_S, multiplexer_2_out, ram_1_dout;

  Clock clock_1 (.out(clock_1_out));
  not not_1 (not_1_out, clock_1_out);
  Register register_1 (.D(B_U_S), .en(A_In), .clk(clock_2_out), .Q(A), .clr(RST));
  Clock clock_2 (.out(clock_2_out));
  Register register_2 (.D(B_U_S), .en(B_In), .clk(clock_3_out), .Q(B), .clr(RST));
  Clock clock_3 (.out(clock_3_out));
  Clock clock_4 (.out(clock_4_out));
  Clock clock_5 (.out(clock_5_out));
  ALU alu_1 (.in_1(A), .in_2(B), .in_3({Alu_Mode_2, Alu_Mode_1}), .out_4(alu_1_out_4));
  Register register_3 (.D(B_U_S), .en(Instruction_In), .clk(clock_4_out), .Q({Instructions, register_3_q}), .clr(RST));
  Register #(.width(4)) register_4 (.D(B_U_S[3:0]), .en(Ram_Adr_In), .clk(clock_5_out), .Q(register_4_q), .clr(RST));
  Counter #(.max('h7), .width(3)) counter_1 (
    .Q(counter_1_q), .clk(not_1_out), .clr(or_1_out));  // open: load, D, count, carry, up
  or or_1 (or_1_out, RST, decoder_1_out5);
  assign B_U_S = A_Out ? A : 8'bz;  // Controlled_Buffer controlled_buffer_1
  assign B_U_S = B_Out ? B : 8'bz;  // Controlled_Buffer controlled_buffer_2
  assign B_U_S = Alu_Out ? alu_1_out_4 : 8'bz;  // Controlled_Buffer controlled_buffer_3
  Counter #(.max('hf), .width(4)) counter_2 (
    .load(Count_Jump), .D(B_U_S[3:0]), .count(Count_En), .Q(Count), .clk(clock_6_out), .clr(RST));  // open: carry, up
  Clock clock_6 (.out(clock_6_out));
  Decoder #(.select(3)) decoder_1 (
    .out5(decoder_1_out5), .sel(counter_1_q));  // open: out0, out1, out2, out3, out4, out6, out7, en
  ROM #(.addrWidth(7), .dataWidth(16)) rom_1 (
    .addr({Instructions, counter_1_q}),
    .data({A_In, A_Out, B_In, Alu_Mode_1, Alu_Mode_2, Alu_Out, Count_En, Count_Out, Count_Jump, Instruction_In, Instruction_Out, Ram_Adr_In, Ram_Data_In, Ram_Data_Out, Output_In, HLT}));
  assign B_U_S = Count_Out ? {4'b0000, Count} : 8'bz;  // Controlled_Buffer controlled_buffer_4
  Clock clock_7 (.out(clock_7_out));
  Button button_1 (.out(button_1_out));
  Multiplexer #(.width(4)) multiplexer_1 (.in0(in_1), .in1(register_4_q), .out(multiplexer_1_out), .sel(in_2));
  Multiplexer #(.width(8)) multiplexer_2 (.in0({in_3, in_4}), .in1(B_U_S), .out(multiplexer_2_out), .sel(in_2));
  Multiplexer multiplexer_3 (.in0(in_5), .in1(Ram_Data_In), .out(multiplexer_3_out), .sel(in_2));
  Register register_5 (.D(B_U_S), .en(Output_In), .clk(clock_8_out), .Q(out_6), .clr(RST));
  Clock clock_8 (.out(clock_8_out));
  or or_2 (or_2_out, clock_7_out, button_1_out);
  RAM #(.addrWidth(4), .asyncread("true")) ram_1 (
    .addr(multiplexer_1_out), .we(multiplexer_3_out), .clk(or_2_out), .din(multiplexer_2_out),
    .dout(ram_1_dout));  // open: oe
  assign B_U_S = Instruction_Out ? {4'b0000, register_3_q} : 8'bz;  // Controlled_Buffer controlled_buffer_5
  assign B_U_S = Ram_Data_Out ? ram_1_dout : 8'bz;  // Controlled_Buffer controlled_buffer_6
  Button button_2 (.out(RST));
  LED led_1 (.in(HLT));
  Clock clock_9 ();  // open: out

  // Other names for the same wires on the sheet: ANS[7:0] = out_6

  // Notes on the sheet:
  //   contents of rom_1 (hex, n*v repeats v):
  //   110 244 6*0 110 244 30 8004 4*0 110 244 30 2004 8400 0 0 0 110 244 30 2004 9400 0 0 0 110 244 30
  //   2004 8c00 0 0 0 110 244 30 2004 9c00 0 0 0 110 244 6*0 110 244 6*0 110 244 6*0 110 244 6*0 110 244
  //   6*0 110 244 6*0 110 244 6*0 110 244 6*0 110 244 4002 5*0 110 244 1
endmodule

module ALU (
  input  [7:0] in_1,
  input  [7:0] in_2,
  input  [1:0] in_3,
  output [7:0] out_4
);

  wire [7:0] adder_1_out, and_1_out, or_1_out, subtractor_1_out;

  Adder adder_1 (.a(in_1), .b(in_2), .out(adder_1_out));  // open: cin, cout
  Subtractor subtractor_1 (.a(in_1), .b(in_2), .out(subtractor_1_out));  // open: bin, bout
  assign and_1_out = in_1 & in_2;  // AND_Gate and_1, 8 bits wide
  assign or_1_out = in_1 | in_2;  // OR_Gate or_1, 8 bits wide
  Multiplexer #(.select(2), .width(8)) multiplexer_1 (
    .in0(adder_1_out), .in1(subtractor_1_out), .in2(and_1_out), .in3(or_1_out), .out(out_4), .sel(in_3));
endmodule

module G (
  input  [3:0] in_1,
  input  [2:0] in_2,
  input  in_3,
  input  [7:0] in_4,
  input  [7:0] in_5
);

  wire clock_1_out, I_1, I_2, I_3, I_4, I_5, I_6, I_7, I_8, I_9, I_10, I_11, I_12, I_13, I_14, I_15, I_16;

  RAM #(.addrWidth(7), .asyncread("true"), .dataWidth(16)) ram_1 (
    .addr({in_1, in_2}), .we(in_3), .clk(clock_1_out), .din({in_4, in_5}),
    .dout({I_1, I_2, I_3, I_4, I_5, I_6, I_7, I_8, I_9, I_10, I_11, I_12, I_13, I_14, I_15, I_16}));  // open: oe
  Clock clock_1 (.out(clock_1_out));
endmodule
